// Logisim project EP01.circ as structural Verilog: 4 circuits, main circuit Somador Completo
module Calculadora_Hexa (
  input  A0,
  input  Ci,
  input  A1,
  input  A2,
  input  A3,
  input  B0,
  input  B1,
  input  B2,
  input  B3,
  output S0,
  output S1,
  output Overflow,
  output S2,
  output Co,
  output S3
);

  wire decodificador_1_a, decodificador_1_b, decodificador_1_c, decodificador_1_d, decodificador_1_e,
       decodificador_1_f, decodificador_1_g, decodificador_2_a, decodificador_2_b, decodificador_2_c,
       decodificador_2_d, decodificador_2_e, decodificador_2_f, decodificador_2_g, decodificador_3_a,
       decodificador_3_b, decodificador_3_c, decodificador_3_d, decodificador_3_e, decodificador_3_f,
       decodificador_3_g;

  Decodificador decodificador_1 (
    .A3(A0), .A2(A1), .A1(A2), .a(decodificador_1_a), .A0(A3), .b(decodificador_1_b), .c(decodificador_1_c),
    .d(decodificador_1_d), .e(decodificador_1_e), .f(decodificador_1_f), .g(decodificador_1_g));
  somador_4bits somador_4bits_1 (
    .Co(Co), .Ci(Ci), .B3(B3), .A3(A3), .B2(B2), .A2(A2), .B1(B1), .A1(A1), .B0(B0), .A0(A0), .S3(S3),
    .S2(S2), .S1(S1), .S0(S0), .Overflow(Overflow));
  Decodificador decodificador_2 (
    .A3(B0), .A2(B1), .A1(B2), .a(decodificador_2_a), .A0(B3), .b(decodificador_2_b), .c(decodificador_2_c),
    .d(decodificador_2_d), .e(decodificador_2_e), .f(decodificador_2_f), .g(decodificador_2_g));
  _7_Segment_Display u_7_segment_display_1 (
    .g(decodificador_1_g), .f(decodificador_1_f), .a(decodificador_1_a), .b(decodificador_1_b),
    .e(decodificador_1_e), .d(decodificador_1_d), .c(decodificador_1_c));  // open: dp
  _7_Segment_Display u_7_segment_display_2 (
    .g(decodificador_2_g), .f(decodificador_2_f), .a(decodificador_2_a), .b(decodificador_2_b),
    .e(decodificador_2_e), .d(decodificador_2_d), .c(decodificador_2_c));  // open: dp
  _7_Segment_Display u_7_segment_display_3 (
    .g(decodificador_3_g), .f(decodificador_3_f), .a(decodificador_3_a), .b(decodificador_3_b),
    .e(decodificador_3_e), .d(decodificador_3_d), .c(decodificador_3_c));  // open: dp
  Decodificador decodificador_3 (
    .A3(S0), .A2(S1), .A1(S2), .a(decodificador_3_a), .A0(S3), .b(decodificador_3_b), .c(decodificador_3_c),
    .d(decodificador_3_d), .e(decodificador_3_e), .f(decodificador_3_f), .g(decodificador_3_g));
endmodule

module Decodificador (
  input  A3,
  input  A2,
  input  A1,
  input  A0,
  output a,
  output b,
  output c,
  output d,
  output e,
  output f,
  output g
);

  wire and_1_out, and_2_out, and_3_out, and_4_out, and_5_out, and_6_out, and_7_out, and_8_out, and_9_out,
       and_10_out, and_11_out, and_12_out, and_13_out, and_14_out, and_15_out, and_16_out, and_17_out,
       and_18_out, and_19_out, and_20_out, and_21_out, and_22_out, and_23_out, and_24_out, and_25_out,
       and_26_out, and_27_out, and_28_out, and_29_out, and_30_out, and_31_out, and_32_out, and_33_out,
       and_34_out, not_1_out, not_2_out, not_3_out, not_4_out, not_5_out, not_6_out, not_7_out, not_8_out,
       not_9_out, not_10_out, not_11_out, not_12_out, not_13_out, not_14_out, not_15_out, not_16_out,
       not_17_out, not_18_out, not_19_out, not_20_out, not_21_out, not_22_out, not_23_out, not_24_out,
       not_25_out, not_26_out, not_27_out, not_28_out, not_29_out, not_30_out, not_31_out, not_32_out,
       not_33_out, not_34_out, not_35_out, not_36_out, not_37_out, not_38_out, not_39_out, not_40_out,
       not_41_out, not_42_out;

  not not_1 (not_1_out, A3);
  and and_1 (and_1_out, not_1_out, not_2_out);
  not not_2 (not_2_out, A1);
  not not_3 (not_3_out, A3);
  and and_2 (and_2_out, not_3_out, A0);
  not not_4 (not_4_out, A2);
  not not_5 (not_5_out, A1);
  and and_3 (and_3_out, not_4_out, not_5_out, A0);
  and and_4 (and_4_out, A2, not_6_out);
  not not_6 (not_6_out, A0);
  and and_5 (and_5_out, A2, A1);
  and and_6 (and_6_out, A3, A1, not_7_out);
  not not_7 (not_7_out, A0);
  not not_8 (not_8_out, A3);
  not not_9 (not_9_out, A2);
  and and_7 (and_7_out, not_8_out, not_9_out, not_10_out);
  not not_10 (not_10_out, A0);
  not not_11 (not_11_out, A3);
  and and_8 (and_8_out, not_11_out, not_12_out);
  not not_12 (not_12_out, A1);
  not not_13 (not_13_out, A2);
  and and_9 (and_9_out, not_13_out, not_14_out);
  not not_14 (not_14_out, A1);
  not not_15 (not_15_out, A2);
  and and_10 (and_10_out, A3, not_15_out, A0);
  and and_11 (and_11_out, A3, A2, not_16_out);
  not not_16 (not_16_out, A0);
  not not_17 (not_17_out, A2);
  and and_12 (and_12_out, not_17_out, not_18_out);
  not not_18 (not_18_out, A1);
  not not_19 (not_19_out, A1);
  and and_13 (and_13_out, not_19_out, A0);
  and and_14 (and_14_out, A1, not_20_out);
  not not_20 (not_20_out, A0);
  and and_15 (and_15_out, A3, not_21_out);
  not not_21 (not_21_out, A2);
  and and_16 (and_16_out, A3, not_22_out);
  not not_22 (not_22_out, A1);
  not not_23 (not_23_out, A3);
  and and_17 (and_17_out, not_23_out, not_24_out, not_25_out);
  not not_24 (not_24_out, A2);
  not not_25 (not_25_out, A1);
  not not_26 (not_26_out, A3);
  and and_18 (and_18_out, not_26_out, A1, A0);
  not not_27 (not_27_out, A3);
  and and_19 (and_19_out, not_27_out, A2, not_28_out);
  not not_28 (not_28_out, A0);
  not not_29 (not_29_out, A2);
  and and_20 (and_20_out, A3, not_29_out, A1);
  and and_21 (and_21_out, A3, A2, not_30_out);
  not not_30 (not_30_out, A1);
  not not_31 (not_31_out, A3);
  and and_22 (and_22_out, not_31_out, not_32_out);
  not not_32 (not_32_out, A1);
  and and_23 (and_23_out, A1, A0);
  not not_33 (not_33_out, A3);
  and and_24 (and_24_out, not_33_out, A2);
  and and_25 (and_25_out, A2, A0);
  not not_34 (not_34_out, A3);
  and and_26 (and_26_out, not_34_out, not_35_out);
  not not_35 (not_35_out, A2);
  not not_36 (not_36_out, A1);
  and and_27 (and_27_out, not_36_out, A0);
  and and_28 (and_28_out, A1, not_37_out);
  not not_37 (not_37_out, A0);
  and and_29 (and_29_out, A2, A1);
  not not_38 (not_38_out, A1);
  and and_30 (and_30_out, not_38_out, A0);
  not not_39 (not_39_out, A2);
  and and_31 (and_31_out, not_39_out, A1, not_40_out);
  not not_40 (not_40_out, A0);
  not not_41 (not_41_out, A3);
  and and_32 (and_32_out, not_41_out, A2);
  and and_33 (and_33_out, A2, not_42_out);
  not not_42 (not_42_out, A1);
  and and_34 (and_34_out, A3, A0);
  or or_1 (b, and_7_out, and_8_out, and_9_out, and_10_out, and_11_out);
  or or_2 (c, and_12_out, and_13_out, and_14_out, and_15_out, and_16_out);
  or or_3 (d, and_17_out, and_18_out, and_19_out, and_20_out, and_21_out);
  or or_4 (e, and_22_out, and_23_out, and_24_out, and_25_out);
  or or_5 (f, and_26_out, and_27_out, and_28_out, and_29_out);
  or or_6 (g, and_30_out, and_31_out, and_32_out, and_33_out, and_34_out);
  or or_7 (a, and_1_out, and_2_out, and_3_out, and_4_out, and_5_out, and_6_out);
endmodule

module somador_4bits (
  input  B3,
  input  A3,
  input  B2,
  input  A2,
  input  B1,
  input  A1,
  input  B0,
  input  A0,
  input  Ci,
  output Co,
  output S3,
  output S2,
  output S1,
  output S0,
  output Overflow
);

  wire somador_completo_2_co0, somador_completo_3_co0, somador_completo_4_co0;

  Somador_Completo somador_completo_1 (.A0(A3), .B0(B3), .Ci0(somador_completo_2_co0), .S0(S3), .Co0(Co));
  xor xor_1 (Overflow, Co, somador_completo_2_co0);
  Somador_Completo somador_completo_2 (
    .A0(A2), .B0(B2), .Ci0(somador_completo_3_co0), .S0(S2), .Co0(somador_completo_2_co0));
  Somador_Completo somador_completo_3 (
    .A0(A1), .B0(B1), .Ci0(somador_completo_4_co0), .S0(S1), .Co0(somador_completo_3_co0));
  Somador_Completo somador_completo_4 (.A0(A0), .B0(B0), .Ci0(Ci), .S0(S0), .Co0(somador_completo_4_co0));
endmodule

module Somador_Completo (
  input  A0,
  input  B0,
  input  Ci0,
  output S0,
  output Co0
);

  wire and_1_out, and_2_out, xor_1_out;

  xor xor_1 (xor_1_out, A0, B0);
  and and_1 (and_1_out, A0, B0);
  xor xor_2 (S0, xor_1_out, Ci0);
  and and_2 (and_2_out, xor_1_out, Ci0);
  or or_1 (Co0, and_2_out, and_1_out);
endmodule
